# Fritzing sketch light_sensor_sketch (saved by Fritzing 0.7.5b)
breadboards: 1

parts:
  Arduino1 = Arduino
  R1 = Photocell (LDR) [package=THT]
  R2 = Resistor [tolerance=±5% resistance=220 package=THT]  # not connected

nets:
  N1: Arduino1.+5V, R1.pin_0
  N2: Arduino1.A0, R1.pin_1

// code stored in the sketch: Kickled_3_pin10_12.ino
/*
  Blink
  Turns on an LED on for one second, then off for one second, repeatedly.
 
  This example code is in the public domain.
 */
 
// Pin 13 has an LED connected on most Arduino boards.
// give it a name:
int led1 = 12;
int led2 = 11;
int led3 = 10;

// the setup routine runs once when you press reset:
void setup() {                
  // initialize the digital pin as an output.
  pinMode(led1, OUTPUT);
  pinMode(led2, OUTPUT); 
  pinMode(led3, OUTPUT); 

}

// the loop routine runs over and over again forever:
void loop() {
  digitalWrite(led1, HIGH);   // turn the LED on (HIGH is the voltage level)
  digitalWrite(led2, HIGH);
  digitalWrite(led3, HIGH);
  delay(500);               // wait for a second
  digitalWrite(led1, LOW);    // turn the LED off by making the voltage LOW
  digitalWrite(led2, LOW);
  digitalWrite(led3, LOW);
  
  //digitalWrite(led3, LOW);
  delay(500);               // wait for a second
}
